# Fritzing sketch PasscodeLock (saved by Fritzing 0.9.0b)
breadboards: 1

parts:
  KEYPAD1 = Membrane Matrix Keypad
  LCD1 = LCD screen
  Part1 = Arduino Uno (Rev3) - ICSP
  R1 = Resistor [tolerance=±5% resistance=220 package=THT]
  POT1 = Breadboard Trimpot
  NEOPIXEL1 = Neopixel Strip -- White (30/m)

nets:
  N1: KEYPAD1.1, Part1.D10_PWM/SS
  N2: KEYPAD1.2, Part1.D11_PWM/MOSI
  N3: KEYPAD1.3, Part1.D12/MISO
  N4: KEYPAD1.4, Part1.D13/SCK
  N5: KEYPAD1.5, Part1.A2
  N6: KEYPAD1.6, Part1.A1
  N7: KEYPAD1.7, Part1.A0
  GND: LCD1.VSS, Part1.GND, R1.Pin_0, POT1.PIN1, NEOPIXEL1.GND
  VDD: LCD1.VDD, LCD1.LED+, Part1.5V, POT1.PIN3, NEOPIXEL1.+5V
  N8: LCD1.V0, POT1.PIN2
  N9: LCD1.RS, Part1.D2
  N10: LCD1.R/W, Part1.D3_PWM
  N11: LCD1.E, Part1.D4
  N12: LCD1.DB4, Part1.D5_PWM
  N13: LCD1.DB5, Part1.D6_PWM
  N14: LCD1.DB6, Part1.D7
  N15: LCD1.DB7, Part1.D8
  N16: LCD1.LED-, R1.Pin_1
  N17: Part1.D9_PWM, NEOPIXEL1.Din

custom parts:
  Membrane Matrix Keypad: Membrane Matrix 3x4 Keypad
  Neopixel Strip -- White (30/m): These NeoPixel strips have 30 digitally-addressable pixel LEDs per meter and are very affordable and are only 12.5 mm wide, 10 mm if you remove the strip from the casing.
